# Fritzing sketch dc_motor_joystick (saved by Fritzing 0.9.4)
breadboards: 1

parts:
  YwRobot_Power_Supply1 = YwRobot Breadboard Power Supply [part_number=545043]
  Part1 = Arduino Uno (Rev3)
  IC1 = L293D [package=THT]
  M1 = DC Motor
  Part2 = KY-023 Dual Axis Joystick Module [package="Breakout board"]

nets:
  N1: YwRobot_Power_Supply1.VCC#5, YwRobot_Power_Supply1.VCC#6
  N2: YwRobot_Power_Supply1.VCC#9, YwRobot_Power_Supply1.VCC#10, IC1.+Vmotor
  N3: YwRobot_Power_Supply1.GND#11, YwRobot_Power_Supply1.GND#12
  GND: YwRobot_Power_Supply1.GND#13, YwRobot_Power_Supply1.GND#14, Part1.GND, IC1.0V, Part2.GND
  N4: Part1.A0, Part2.VRx
  N5: Part1.D8, IC1.In_1
  N6: Part1.D9_PWM, IC1.Enable_1
  N7: Part1.D12/MISO, IC1.In_2
  5V: Part1.5V, Part2.+5V
  N8: IC1.Out_1_(_Controlled_by_Enable_1_), M1.pin_2
  N9: IC1.Out_2_(_Controlled_by_Enable_1_), M1.pin_1

custom parts:
  YwRobot Breadboard Power Supply: The YwRobot Breadboard Power Supply (MB-V2) has two power rails; they can be 5V or 3V3. Power to the module can be provided through the female USB socket or through the A10 (female) 2.1mm power jack.
  KY-023 Dual Axis Joystick Module: X/Y Analog Joystick KEYES KY-023 module. It contains two potentiometers and a button.
