# Fritzing sketch shift_register (saved by Fritzing 0.9.4)
breadboards: 1

parts:
  Part1 = Arduino Uno (Rev3)
  U1 = 74HC595 [package="DIP16 [THT]"]
  LED1 = smd LED [color="Red (633nm)" package="1206 [SMD]"]
  LED2 = smd LED [color="Red (633nm)" package="1206 [SMD]"]
  LED3 = smd LED [color="Red (633nm)" package="1206 [SMD]"]
  LED4 = smd LED [color="Red (633nm)" package="1206 [SMD]"]
  LED5 = smd LED [color="Green (555nm)" package="1206 [SMD]"]
  LED6 = smd LED [color="Green (555nm)" package="1206 [SMD]"]
  LED7 = smd LED [color="Green (555nm)" package="1206 [SMD]"]
  LED8 = smd LED [color="Green (555nm)" package="1206 [SMD]"]
  R1 = Resistor [tolerance=±5% resistance=220 package="0603 [SMD]"]
  R2 = Resistor [tolerance=±5% resistance=220 package="0603 [SMD]"]
  R3 = Resistor [tolerance=±5% resistance=220 package="0603 [SMD]"]
  R4 = Resistor [tolerance=±5% resistance=220 package="0603 [SMD]"]
  R5 = Resistor [tolerance=±5% resistance=220 package="0603 [SMD]"]
  R6 = Resistor [tolerance=±5% resistance=220 package="0603 [SMD]"]
  R7 = Resistor [tolerance=±5% resistance=220 package="0603 [SMD]"]
  R8 = Resistor [tolerance=±5% resistance=220 package="0603 [SMD]"]
  S1 = Momentary Switch [package=ksa_sealed_tac_switch]

nets:
  N1: Part1.D9_PWM, U1.SH_CP
  N2: Part1.D11_PWM/MOSI, U1.ST_CP
  N3: Part1.D12/MISO, U1.DS
  N4: Part1.D2, S1.3
  5V: Part1.5V, U1.VCC
  GND: Part1.GND, U1.GND, U1.MR, U1.OE, LED1.cathode, LED2.cathode, LED3.cathode, LED4.cathode, LED5.cathode, LED6.cathode, LED7.cathode, LED8.cathode, S1.1
  N5: U1.Q1, R7.Pin_1
  N6: U1.Q2, R6.Pin_1
  N7: U1.Q3, R5.Pin_1
  N8: U1.Q4, R4.Pin_1
  N9: U1.Q5, R3.Pin_1
  N10: U1.Q6, R2.Pin_1
  N11: U1.Q7, R1.Pin_1
  N12: U1.Q0, R8.Pin_1
  N13: LED1.anode, R1.Pin_0
  N14: LED2.anode, R2.Pin_0
  N15: LED3.anode, R3.Pin_0
  N16: LED4.anode, R4.Pin_0
  N17: LED5.anode, R5.Pin_0
  N18: LED6.anode, R6.Pin_0
  N19: LED7.anode, R7.Pin_0
  N20: LED8.anode, R8.Pin_0
